// Logisim project AddersCollection.circ as structural Verilog: 4 circuits, main circuit 1bit_adder
module _1bit_adder (
  input  A,
  input  B,
  input  C,
  output S,
  output P
);

  wire and_1_out, and_2_out, xor_1_out;

  xor xor_1 (xor_1_out, A, B);
  and and_1 (and_1_out, C, xor_1_out);
  and and_2 (and_2_out, B, A);
  xor xor_2 (S, xor_1_out, C);
  or or_1 (P, and_1_out, and_2_out);
endmodule

module _4bit_adder (
  input  A0,
  input  A1,
  input  A2,
  input  A3,
  input  P0,
  input  B0,
  input  B1,
  input  B2,
  input  B3,
  output S0,
  output S1,
  output S2,
  output S3,
  output P
);

  wire n1bit_adder_1_p, n1bit_adder_2_p, n1bit_adder_3_p;

  _1bit_adder u_1bit_adder_1 (.A(A0), .B(B0), .C(P0), .S(S0), .P(n1bit_adder_1_p));
  _1bit_adder u_1bit_adder_2 (.A(A1), .B(B1), .C(n1bit_adder_1_p), .S(S1), .P(n1bit_adder_2_p));
  _1bit_adder u_1bit_adder_3 (.A(A2), .B(B2), .C(n1bit_adder_2_p), .S(S2), .P(n1bit_adder_3_p));
  _1bit_adder u_1bit_adder_4 (.A(A3), .B(B3), .C(n1bit_adder_3_p), .S(S3), .P(P));
endmodule

module _16bit_adder (
  input  A0,
  input  A1,
  input  A2,
  input  A3,
  input  A4,
  input  A5,
  input  A6,
  input  A7,
  input  A8,
  input  A9,
  input  A10,
  input  A11,
  input  A12,
  input  A13,
  input  A14,
  input  A15,
  input  P0,
  input  B0,
  input  B1,
  input  B2,
  input  B3,
  input  B4,
  input  B5,
  input  B6,
  input  B7,
  input  B8,
  input  B9,
  input  B10,
  input  B11,
  input  B12,
  input  B13,
  input  B14,
  input  B15,
  output C0,
  output C1,
  output C2,
  output C3,
  output C4,
  output C5,
  output C6,
  output C7,
  output C8,
  output C9,
  output C10,
  output C11,
  output C12,
  output C13,
  output C14,
  output C15,
  output P
);

  wire n4bit_adder_1_p, n4bit_adder_2_p, n4bit_adder_3_p;

  _4bit_adder u_4bit_adder_1 (
    .A0(A0), .A1(A1), .A2(A2), .A3(A3), .P0(P0), .B0(B0), .B1(B1), .B2(B2), .B3(B3), .S0(C0), .S1(C1),
    .S2(C2), .S3(C3), .P(n4bit_adder_1_p));
  _4bit_adder u_4bit_adder_2 (
    .A0(A4), .A1(A5), .A2(A6), .A3(A7), .P0(n4bit_adder_1_p), .B0(B4), .B1(B5), .B2(B6), .B3(B7), .S0(C4),
    .S1(C5), .S2(C6), .S3(C7), .P(n4bit_adder_2_p));
  _4bit_adder u_4bit_adder_3 (
    .A0(A8), .A1(A9), .A2(A10), .A3(A11), .P0(n4bit_adder_2_p), .B0(B8), .B1(B9), .B2(B10), .B3(B11),
    .S0(C8), .S1(C9), .S2(C10), .S3(C11), .P(n4bit_adder_3_p));
  _4bit_adder u_4bit_adder_4 (
    .A0(A12), .A1(A13), .A2(A14), .A3(A15), .P0(n4bit_adder_3_p), .B0(B12), .B1(B13), .B2(B14), .B3(B15),
    .S0(C12), .S1(C13), .S2(C14), .S3(C15), .P(P));
endmodule

module _64bit_adder (
  input  A0,
  input  A1,
  input  A2,
  input  A3,
  input  A4,
  input  A5,
  input  A6,
  input  A7,
  input  A8,
  input  A9,
  input  A10,
  input  A11,
  input  A12,
  input  A13,
  input  A14,
  input  A15,
  input  A16,
  input  A17,
  input  A18,
  input  A19,
  input  A20,
  input  A21,
  input  A22,
  input  A23,
  input  A24,
  input  A25,
  input  A26,
  input  A27,
  input  A28,
  input  A29,
  input  A30,
  input  A31,
  input  A32,
  input  A33,
  input  A34,
  input  A35,
  input  A36,
  input  A37,
  input  A38,
  input  A39,
  input  A40,
  input  A41,
  input  A42,
  input  A43,
  input  A44,
  input  A45,
  input  A46,
  input  A47,
  input  A48,
  input  A49,
  input  A50,
  input  A51,
  input  A52,
  input  A53,
  input  A54,
  input  A55,
  input  A56,
  input  A57,
  input  A58,
  input  A59,
  input  A60,
  input  A61,
  input  A62,
  input  A63,
  input  P0,
  input  B0,
  input  B1,
  input  B2,
  input  B3,
  input  B4,
  input  B5,
  input  B6,
  input  B7,
  input  B8,
  input  B9,
  input  B10,
  input  B11,
  input  B12,
  input  B13,
  input  B14,
  input  B15,
  input  B16,
  input  B17,
  input  B18,
  input  B19,
  input  B20,
  input  B21,
  input  B22,
  input  B23,
  input  B24,
  input  B25,
  input  B26,
  input  B27,
  input  B28,
  input  B29,
  input  B30,
  input  B31,
  input  B32,
  input  B33,
  input  B34,
  input  B35,
  input  B36,
  input  B37,
  input  B38,
  input  B39,
  input  B40,
  input  B41,
  input  B42,
  input  B43,
  input  B44,
  input  B45,
  input  B46,
  input  B47,
  input  B48,
  input  B49,
  input  B50,
  input  B51,
  input  B52,
  input  B53,
  input  B54,
  input  B55,
  input  B56,
  input  B57,
  input  B58,
  input  B59,
  input  B60,
  input  B61,
  input  B62,
  input  B63,
  output C0,
  output C1,
  output C2,
  output C3,
  output C4,
  output C5,
  output C6,
  output C7,
  output C8,
  output C9,
  output C10,
  output C11,
  output C12,
  output C13,
  output C14,
  output C15,
  output C16,
  output C17,
  output C18,
  output C19,
  output C20,
  output C21,
  output C22,
  output C23,
  output C24,
  output C25,
  output C26,
  output C27,
  output C28,
  output C29,
  output C30,
  output C31,
  output C32,
  output C33,
  output C34,
  output C35,
  output C36,
  output C37,
  output C38,
  output C39,
  output C40,
  output C41,
  output C42,
  output C43,
  output C44,
  output C45,
  output C46,
  output C47,
  output C48,
  output C49,
  output C50,
  output C51,
  output C52,
  output C53,
  output C54,
  output C55,
  output C56,
  output C57,
  output C58,
  output C59,
  output C60,
  output C61,
  output C62,
  output C63,
  output P
);

  wire n16bit_adder_1_p, n16bit_adder_2_p, n16bit_adder_3_p;

  _16bit_adder u_16bit_adder_1 (
    .A0(A0), .A1(A1), .A2(A2), .A3(A3), .A4(A4), .A5(A5), .A6(A6), .A7(A7), .A8(A8), .A9(A9), .A10(A10),
    .A11(A11), .A12(A12), .A13(A13), .A14(A14), .A15(A15), .P0(P0), .B0(B0), .B1(B1), .B2(B2), .B3(B3),
    .B4(B4), .B5(B5), .B6(B6), .B7(B7), .B8(B8), .B9(B9), .B10(B10), .B11(B11), .B12(B12), .B13(B13),
    .B14(B14), .B15(B15), .C0(C0), .C1(C1), .C2(C2), .C3(C3), .C4(C4), .C5(C5), .C6(C6), .C7(C7), .C8(C8),
    .C9(C9), .C10(C10), .C11(C11), .C12(C12), .C13(C13), .C14(C14), .C15(C15), .P(n16bit_adder_1_p));
  _16bit_adder u_16bit_adder_2 (
    .A0(A16), .A1(A17), .A2(A18), .A3(A19), .A4(A20), .A5(A21), .A6(A22), .A7(A23), .A8(A24), .A9(A25),
    .A10(A26), .A11(A27), .A12(A28), .A13(A29), .A14(A30), .A15(A31), .P0(n16bit_adder_1_p), .B0(B16),
    .B1(B17), .B2(B18), .B3(B19), .B4(B20), .B5(B21), .B6(B22), .B7(B23), .B8(B24), .B9(B25), .B10(B26),
    .B11(B27), .B12(B28), .B13(B29), .B14(B30), .B15(B31), .C0(C16), .C1(C17), .C2(C18), .C3(C19), .C4(C20),
    .C5(C21), .C6(C22), .C7(C23), .C8(C24), .C9(C25), .C10(C26), .C11(C27), .C12(C28), .C13(C29), .C14(C30),
    .C15(C31), .P(n16bit_adder_2_p));
  _16bit_adder u_16bit_adder_3 (
    .A0(A32), .A1(A33), .A2(A34), .A3(A35), .A4(A36), .A5(A37), .A6(A38), .A7(A39), .A8(A40), .A9(A41),
    .A10(A42), .A11(A43), .A12(A44), .A13(A45), .A14(A46), .A15(A47), .P0(n16bit_adder_2_p), .B0(B32),
    .B1(B33), .B2(B34), .B3(B35), .B4(B36), .B5(B37), .B6(B38), .B7(B39), .B8(B40), .B9(B41), .B10(B42),
    .B11(B43), .B12(B44), .B13(B45), .B14(B46), .B15(B47), .C0(C32), .C1(C33), .C2(C34), .C3(C35), .C4(C36),
    .C5(C37), .C6(C38), .C7(C39), .C8(C40), .C9(C41), .C10(C42), .C11(C43), .C12(C44), .C13(C45), .C14(C46),
    .C15(C47), .P(n16bit_adder_3_p));
  _16bit_adder u_16bit_adder_4 (
    .A0(A48), .A1(A49), .A2(A50), .A3(A51), .A4(A52), .A5(A53), .A6(A54), .A7(A55), .A8(A56), .A9(A57),
    .A10(A58), .A11(A59), .A12(A60), .A13(A61), .A14(A62), .A15(A63), .P0(n16bit_adder_3_p), .B0(B48),
    .B1(B49), .B2(B50), .B3(B51), .B4(B52), .B5(B53), .B6(B54), .B7(B55), .B8(B56), .B9(B57), .B10(B58),
    .B11(B59), .B12(B60), .B13(B61), .B14(B62), .B15(B63), .C0(C48), .C1(C49), .C2(C50), .C3(C51), .C4(C52),
    .C5(C53), .C6(C54), .C7(C55), .C8(C56), .C9(C57), .C10(C58), .C11(C59), .C12(C60), .C13(C61), .C14(C62),
    .C15(C63), .P(P));
endmodule
